// Logisim project multiplier.circ as structural Verilog: 1 circuit, main circuit main
module main (
  input  in_1,
  input  in_2,
  input  [7:0] in_3,
  input  [7:0] in_4,
  output [7:0] out_5
);

  wire bitselector_1_out;
  wire [2:0] counter_1_q;
  wire [7:0] adder_1_out, multiplexer_1_out, shifter_1_out;

  Register register_1 (.D(adder_1_out), .Q(out_5), .clk(in_1));  // open: en, clr
  Counter #(.width(3), .max('h7)) counter_1 (.Q(counter_1_q), .carry(in_2), .clk(in_1));  // open: load, D, count, clr
  BitSelector bitselector_1 (.in(in_3), .out(bitselector_1_out), .sel(counter_1_q));
  Adder adder_1 (.a(out_5), .b(multiplexer_1_out), .out(adder_1_out));  // open: cin, cout
  Shifter shifter_1 (.in(in_4), .\dist (counter_1_q), .out(shifter_1_out));
  Multiplexer #(.width(8), .enable("false")) multiplexer_1 (
    .in1(shifter_1_out), .out(multiplexer_1_out), .sel(bitselector_1_out));  // open: in0
endmodule
